# Fritzing sketch diagrama (saved by Fritzing 0.9.4)

parts:
  Componente1 = Arduino Uno (Rev3) - ICSP
  BT1 = Bluetooth HC-06u [package=THT]

nets:
  N1: Componente1.D10_PWM/SS, BT1.TXD
  N2: Componente1.D11_PWM/MOSI, BT1.RXD
  5V: Componente1.5V, BT1.VCC
  GND: Componente1.GND, BT1.GND

custom parts:
  Bluetooth HC-06u: Bluetooth HC-06 - face up, pins down 16.5mm x 37.5mm PCB
