# Fritzing sketch rfid (saved by Fritzing 0.9.4)

parts:
  U1 = RFID RC522 SIP - 8 pins [chip_label="RFID RC522" package="SIP (Single Inline) [THT]"]
  Componente1 = Arduino Uno (Rev3) - ICSP

nets:
  N1: U1.IRQ, Componente1.D10_PWM/SS
  N2: U1.NSS, Componente1.D13/SCK
  N3: U1.SCK, Componente1.D11_PWM/MOSI
  N4: U1.MOSI, Componente1.D12/MISO
  GND: U1.GND, Componente1.GND
  N5: U1.RST, Componente1.D9_PWM
  VCC: U1.VCC, Componente1.3V3

custom parts:
  RFID RC522 SIP - 8 pins: A SIP stand-in part for RFID RC522 . With 8 pins on a 300 mil single inline package (SIP) footprint.
